# Fritzing sketch breadboard (saved by Fritzing 0.9.4)
breadboards: 1

parts:
  S1 = Toggle Switch [package=THT]
  M1 = RioRand LM2596
  Hybrid_Circuit3 = JY-MCU 3V-5V Bidirectional Level Shifter [package="DIP (Dual Inline)"]
  Hybrid_Circuit5 = JY-MCU 3V-5V Bidirectional Level Shifter [package="DIP (Dual Inline)"]
  JACK1 = 2.1mm Barrel Jack with Terminal Block
  U1 = NodeMCU V3.0
  TRM1 = Terminal 2pin
  Q1 = MOSFET-NCHANNEL [package=to220v]
  U2 = 4RelayModule
  NEOPIXEL2 = Neopixel Strip -- Black (60/m) [part_number=1461]
  LED1 = LEDs [package=led10mm]

nets:
  N1: S1.L1, U1.D7
  N2: S1.COM, M1.Pin_4, Hybrid_Circuit3.GND, Hybrid_Circuit5.GND#10, U1.GND#6, U1.GND#13, U1.GND#16, U1.GND#33
  VCC: M1.Pin_1, JACK1.POS, U2.VCC, NEOPIXEL2.+5V
  N3: M1.Pin_2, JACK1.NEG, U2.GND
  N4: M1.Pin_3, Hybrid_Circuit3.5Vin, Hybrid_Circuit5.5Vin
  N5: Hybrid_Circuit3.3.3Vout, U1.3V3
  N6: Hybrid_Circuit3.I/O-1L, U1.D6
  N7: Hybrid_Circuit3.I/O-2L, U1.D5
  N8: Hybrid_Circuit3.I/O-3L, U1.D0
  N9: Hybrid_Circuit3.I/O-3H, U2.IN3
  N10: Hybrid_Circuit3.I/O-2H, U2.IN2
  N11: Hybrid_Circuit3.I/O-1H, U2.IN1
  N12: Hybrid_Circuit5.I/O-1L, U1.D2
  N13: Hybrid_Circuit5.I/O-1H, NEOPIXEL2.DI
  N14: U1.D1, Q1.G
  N15: TRM1.pin_1, LED1.A
  N16: TRM1.pin_2, Q1.D, LED1.C

notes:
  12v DC IN
  12v DC Rail
  5v DC Rail
  White LED strip
  WS2811 strip
  White LED Strip Switch

custom parts:
  JY-MCU 3V-5V Bidirectional Level Shifter: JY-MCU 3V-5V Bidirectional Level Shifter with 12 pins on a 500mil dual inline package (DIP) footprint.
  NodeMCU V3.0: ESP8266 based NodeMCU
  Terminal 2pin: 2-pin Terminal Block
  4RelayModule: 4 relay arduino module SONGLE SRD05VDC-SL-C
  Neopixel Strip -- Black (60/m): Neopixel Strip, Black, 60 pixels per meter.
